# Fritzing sketch Rx_Sketch (saved by Fritzing 0.9.3b)

parts:
  U1 = ESP8266 NodeMCU LoLin module
  Part1 = Adafruit RFM9x LoRa Radio [part_number="Adafruit #3072 and #3073"]

nets:
  N1: U1.D0, Part1.RST
  N2: U1.D2, Part1.DIO0
  3V3: U1.3V3, Part1.VIN
  GND: U1.GND, Part1.GND
  N3: U1.D5, Part1.SCK
  N4: U1.D6, Part1.MISO
  N5: U1.D7, Part1.MOSI
  N6: U1.D8, Part1.CS

custom parts:
  ESP8266 NodeMCU LoLin module: ESP8266 based NodeMCU
  Adafruit RFM9x LoRa Radio: Sending data over long distances is like magic, and now you can be a magician with this range of powerful and easy-to-use radio modules. Sure, sometimes you want to talk to a computer (a good time to use WiFi) or perhaps communicate with a Phone (choose Bluetooth Low Energy!) but what if you want to send data very far? Most WiFi, Bluetooth, Zigbee and other wireless chipsets use 2.4GHz, which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
