# Fritzing sketch Tx_Sketch (saved by Fritzing 0.9.3b)

parts:
  U1 = lolin
  Part1 = Adafruit RFM9x LoRa Radio [part_number="Adafruit #3072 and #3073"]

nets (from the breadboard view):
  N1: U1.connector11, Part1.RST
  N2: U1.connector19, Part1.DIO0
  N3: U1.connector20, Part1.GND
  N4: U1.connector25, Part1.VIN
  N5: U1.connector26, Part1.CS
  N6: U1.connector27, Part1.SCK
  N7: U1.connector28, Part1.MOSI
  N8: U1.connector29, Part1.MISO

custom parts:
  Adafruit RFM9x LoRa Radio: Sending data over long distances is like magic, and now you can be a magician with this range of powerful and easy-to-use radio modules. Sure, sometimes you want to talk to a computer (a good time to use WiFi) or perhaps communicate with a Phone (choose Bluetooth Low Energy!) but what if you want to send data very far? Most WiFi, Bluetooth, Zigbee and other wireless chipsets use 2.4GHz, which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
